// Digital circuit alu.dig as structural Verilog
module alu (
  input  clk,
  input  [15:0] A,
  input  [15:0] B,
  input  [1:0] OP,
  input  Write_Z,
  output [15:0] Result,
  output Z
);

  wire comparator_1_eq;
  wire [15:0] add_1_s, and_1_out, not_1_out, or_1_out;

  assign or_1_out = A | B;  // Or or_1, 16 bits wide
  assign and_1_out = A & B;  // And and_1, 16 bits wide
  Add #(.Bits(16)) add_1 (.a(A), .b(B), .c_i(1'b0), .s(add_1_s));  // open: c_o
  assign not_1_out = ~A;  // Not not_1, 16 bits wide
  Multiplexer #(.Selector_Bits(2), .Bits(16)) multiplexer_1 (
    .sel(OP), .in_0(add_1_s), .in_1(or_1_out), .in_2(and_1_out), .in_3(not_1_out), .out(Result));
  Comparator #(.Bits(16)) comparator_1 (.a(Result), .b({16{1'b0}}), .eq(comparator_1_eq));  // open: gt, lt
  Register register_1 (.D(comparator_1_eq), .C(clk), .en(Write_Z), .Q(Z));
endmodule
