// Digital circuit control_unit.dig as structural Verilog
module control_unit (
  input  [15:0] Instr,
  input  Z,
  output [2:0] RF_write_sel,
  output [2:0] RF_read_sel_1,
  output [2:0] RF_read_sel_2,
  output Mem_str,
  output RF_write_en,
  output PC_jump,
  output [7:0] PC_data,
  output [1:0] ALU_op,
  output ALU_z,
  output [15:0] Output_imm,
  output [1:0] Output_sel
);

  wire and_1_out, and_3_out;

  and and_1 (and_1_out, Instr[14], ~Instr[15]);  // And
  and and_2 (Mem_str, Instr[12], ~Instr[13], Instr[14], ~Instr[15]);  // And
  and and_3 (and_3_out, ~Instr[12], Instr[13], ~Instr[14], ~Instr[15]);  // And
  nor nor_1 (Output_sel[1], Instr[15], and_1_out);
  Multiplexer #(.Bits(3)) multiplexer_1 (.sel(Mem_str), .in_0(Instr[2:0]), .in_1(Instr[10:8]), .out(RF_read_sel_2));
  and and_4 (Output_sel[0], ~Instr[15], and_1_out);  // And
  nor nor_2 (RF_write_en, Mem_str, and_3_out);
  and and_5 (PC_jump, and_3_out, ~Z);  // And

  assign ALU_op = Instr[13:12];
  assign ALU_z = Instr[15];
  assign Output_imm = {{8{1'b0}}, Instr[7:0]};
  assign PC_data = Instr[7:0];
  assign RF_read_sel_1 = Instr[6:4];
  assign RF_write_sel = Instr[10:8];
endmodule
