// Digital circuit cpu.dig as structural Verilog
module cpu (
  input  clk
);

  wire alu_1_z, control_unit_1_alu_z, control_unit_1_mem_str, control_unit_1_pc_jump,
       control_unit_1_rf_write_en;
  wire [1:0] control_unit_1_alu_op, control_unit_1_output_sel;
  wire [2:0] control_unit_1_rf_read_sel_1, control_unit_1_rf_read_sel_2, control_unit_1_rf_write_sel;
  wire [7:0] control_unit_1_pc_data;
  wire [15:0] alu_1_result, control_unit_1_output_imm, multiplexer_1_out, notconnected_1_out, pc_1_x,
       ramdualaccess_1_d1, ramdualaccess_1_d2, reg_file_1_read1_out, reg_file_1_read2_out;

  control_unit control_unit_1 (
    .Instr(ramdualaccess_1_d2), .Z(alu_1_z), .RF_write_sel(control_unit_1_rf_write_sel),
    .RF_read_sel_1(control_unit_1_rf_read_sel_1), .RF_read_sel_2(control_unit_1_rf_read_sel_2),
    .Mem_str(control_unit_1_mem_str), .RF_write_en(control_unit_1_rf_write_en),
    .PC_jump(control_unit_1_pc_jump), .PC_data(control_unit_1_pc_data), .ALU_op(control_unit_1_alu_op),
    .ALU_z(control_unit_1_alu_z), .Output_imm(control_unit_1_output_imm),
    .Output_sel(control_unit_1_output_sel));
  pc pc_1 (.clk(clk), .load(control_unit_1_pc_jump), .D(control_unit_1_pc_data), .X(pc_1_x));
  reg_file reg_file_1 (
    .clk(clk), .Write_data(multiplexer_1_out), .Write_en(control_unit_1_rf_write_en),
    .Write_sel(control_unit_1_rf_write_sel), .Read1_sel(control_unit_1_rf_read_sel_1),
    .Read2_sel(control_unit_1_rf_read_sel_2), .Read1_out(reg_file_1_read1_out),
    .Read2_out(reg_file_1_read2_out));
  alu alu_1 (
    .clk(clk), .A(reg_file_1_read1_out), .B(reg_file_1_read2_out), .OP(control_unit_1_alu_op),
    .Write_Z(control_unit_1_alu_z), .Result(alu_1_result), .Z(alu_1_z));
  RAMDualAccess #(.AddrBits(16), .isProgramMemory("true"), .Bits(16)) ramdualaccess_1 (
    .str(control_unit_1_mem_str), .C(clk), .ld(1'b1), .A1(reg_file_1_read1_out), .Din1(reg_file_1_read2_out),
    .A2(pc_1_x), .D1(ramdualaccess_1_d1), .D2(ramdualaccess_1_d2));
  Multiplexer #(.Selector_Bits(2), .Bits(16)) multiplexer_1 (
    .sel(control_unit_1_output_sel), .in_0(alu_1_result), .in_1(ramdualaccess_1_d1),
    .in_2(control_unit_1_output_imm), .in_3(notconnected_1_out), .out(multiplexer_1_out));
  // NotConnected on notconnected_1_out
endmodule
