// Digital circuit pc.dig as structural Verilog
module pc (
  input  clk,
  input  load,
  input  [7:0] D,
  output [15:0] X
);

  wire [15:0] add_1_s, bitextender_1_out, multiplexer_1_out;

  Register #(.Bits(16)) PC (.D(add_1_s), .C(clk), .en(1'b1), .Q(X));
  Add #(.Bits(16)) add_1 (.a(X), .b(multiplexer_1_out), .c_i(1'b0), .s(add_1_s));  // open: c_o
  Multiplexer #(.Bits(16)) multiplexer_1 (.sel(load), .in_0(16'h1), .in_1(bitextender_1_out), .out(multiplexer_1_out));
  BitExtender bitextender_1 (.in(D), .out(bitextender_1_out));
endmodule
